# Fritzing sketch RoboCoop (saved by Fritzing 0.9.2b)
breadboards: 2

parts:
  LCD1 = LCD screen
  Q1 = Basic FET P-Channel [package="TO220 [THT]"]
  Q2 = Basic FET P-Channel [package="TO220 [THT]"]
  Q4 = Basic FET N-Channel [package="TO220 [THT]"]
  Q3 = Basic FET N-Channel [package="TO220 [THT]"]
  D1 = Rectifier Diode [part_number=1N4001 package="300 mil [THT]"]
  D2 = Rectifier Diode [part_number=1N4001 package="300 mil [THT]"]
  VCC1 = 4 x AAA Battery Mount
  D3 = Rectifier Diode [part_number=1N4001 package="300 mil [THT]"]
  D4 = Rectifier Diode [part_number=1N4001 package="300 mil [THT]"]
  M1 = DC Motor
  R1 = Resistor [tolerance=±5% resistance=220 package=THT]
  R2 = Trimmer Potentiometer [maximum_resistance=10kΩ package=THT]
  AND = IC, DIP package, 14 pins [chip_label=7408N]
  NANO = Arduino Nano (Rev3.0)
  Q5 = NPN-Transistor [package="TO92 [THT]"]
  L1 = Solenoid
  D5 = Rectifier Diode [part_number=1N4001 package="300 mil [THT]"]
  R3 = Resistor [tolerance=±5% resistance=1k package=THT]
  R4 = Resistor [tolerance=±5% resistance=1k package=THT]
  USER_SW = Pushbutton [package=THT]
  R5 = Resistor [tolerance=±5% resistance=1k package=THT]
  MICRO_SW = Pushbutton [package=THT]
  SET = Pushbutton [package=THT]
  SELECT = Pushbutton [package=THT]
  R6 = Resistor [tolerance=±5% resistance=1k package=THT]
  R7 = Resistor [tolerance=±5% resistance=1k package=THT]
  NOT = IC, DIP package, 14 pins [chip_label=SN74LS04N]
  C1 = Ceramic Capacitor [capacitance=100nF package="100 mil [THT, multilayer]"]
  C2 = Ceramic Capacitor [capacitance=100nF package="100 mil [THT, multilayer]"]
  C3 = Electrolytic Capacitor [capacitance=1µF package="100 mil [THT, electrolytic]"]

nets:
  VSS: LCD1.VSS, LCD1.LED-, R2.leg1, AND.pin7, NANO.GND, Q5.E, R4.Pin_0, R5.Pin_0, R6.Pin_0, R7.Pin_0, NOT.pin7
  VDD: LCD1.VDD, R1.Pin_0, R2.leg2, AND.pin14, NANO.5V, USER_SW.leg1, MICRO_SW.leg1, SET.leg1, SELECT.leg1, NOT.pin14
  N1: LCD1.V0, R2.wiper
  N2: LCD1.RS, NANO.D8
  N3: LCD1.R/W, NANO.D9
  N4: LCD1.E, NANO.D10
  N5: LCD1.DB4, NANO.D11/MOSI
  N6: LCD1.DB5, NANO.D6
  N7: LCD1.DB6, NANO.D12/MISO
  N8: LCD1.DB7, NANO.D7
  N9: LCD1.LED+, R1.Pin_1
  N10: Q1.gate, NOT.pin6
  N11: Q1.drain, Q4.drain, D1.anode, D4.cathode, M1.pin_1, C1.0
  N12: Q1.source, Q2.source, D1.cathode, D2.cathode, VCC1.+, C3.+
  N13: Q2.gate, NOT.pin12
  N14: Q2.drain, Q3.drain, D2.anode, D3.cathode, M1.pin_2, C1.1
  N15: Q4.gate, AND.pin3, NOT.pin13
  N16: Q4.source, Q3.source, VCC1.-, D3.anode, D4.anode, C3.-
  N17: Q3.gate, AND.pin6, NOT.pin5
  N18: AND.pin1, NANO.D5, NOT.pin1
  N19: AND.pin2, AND.pin5, NANO.D13/SCK
  N20: AND.pin4, NOT.pin2
  N21: NANO.D2, SELECT.leg0, R7.Pin_1
  N22: NANO.D3, SET.leg0, R6.Pin_1
  N23: NANO.A4, R5.Pin_1, MICRO_SW.leg0
  N24: NANO.A3, R4.Pin_1, USER_SW.leg0
  N25: NANO.A2, R3.Pin_1
  N26: Q5.B, R3.Pin_0
  N27: Q5.C, L1.pin1, D5.anode, C2.0
  7V: L1.pin2, D5.cathode, C2.1
